# Fritzing sketch Принципиальная схема (saved by Fritzing 0.9.10b)

parts:
  Raspberry_Pi_1 = Raspberry Pi 3 [part_number=RPI-3-V1.2]
  RPi_Camera_(CSI) = Rasberry Pi NIOR Camera [chip_label=IC package="DIP (Dual Inline) [THT]"]  # not connected
  U1 = LM2596 step down module
  S1 = Round Pushbutton
  GLCD_128x1 = 128 x 64 Graphic LCD  # not connected
  3-pins_Hall_Effect_Sensor1 = mystery part, 3 pins [chip_label="Hall Effect Sensor"]
  S2 = Limit Switch [package="Breakout Board"]
  J1 = Basic Servo
  C1 = Electrolytic Capacitor [capacitance=0.1µF voltage=35V package="100 mil [THT, electrolytic]"]
  WeMos_D1_Mini1 = WeMos D1 Mini
  C2 = Electrolytic Capacitor [capacitance=0.1µF voltage=35V package="100 mil [THT, electrolytic]"]
  U2 = LIPO-2000mAh [package=lipo-2000]
  TP1 = TP4056 [chip_label=TP4056 package="DIP (Dual Inline) [THT]"]
  U3 = LIPO-2000mAh [package=lipo-2000]
  J2 = Basic Servo
  J3 = Basic Servo

nets:
  3V3: Raspberry_Pi_1.3v3, Raspberry_Pi_1.3V3, C1.+
  GND: Raspberry_Pi_1.GND, U1.IN-, U1.OUT-, J1.gnd, C1.-, TP1.pin6, J2.gnd, J3.gnd
  VCC: Raspberry_Pi_1.5V, U1.OUT+, J1.vcc, J2.vcc, J3.vcc
  N1: U1.IN+, S1.leg1
  N2: S1.leg0, TP1.pin3
  N3: 3-pins_Hall_Effect_Sensor1.pin1, S2.G, WeMos_D1_Mini1.G, C2.-
  N4: 3-pins_Hall_Effect_Sensor1.pin2, WeMos_D1_Mini1.3V3
  N5: 3-pins_Hall_Effect_Sensor1.pin3, WeMos_D1_Mini1.D6
  N6: S2.S, WeMos_D1_Mini1.D5
  N7: J1.pulse, WeMos_D1_Mini1.D4
  N8: WeMos_D1_Mini1.5V, C2.+
  N9: WeMos_D1_Mini1.D7, J3.pulse
  N10: WeMos_D1_Mini1.D8, J2.pulse
  N11: U2.+, U3.-
  N12: U2.-, TP1.pin5
  N13: TP1.pin4, U3.+

notes:
  3.5 дюймовый дисплей RPi LCD V3.
  Сенсорный экран соединятеся с Raspberry Pi 4b через пины.
  Дисплей подключается по HDMI
  Raspberry Pi High Quality.
  Соединяется с Raspberry Pi по шине CIS
  Raspberry Pi 4b
  Реализует управление устройством и алгоритмы системы технического зрения
  ESP 8266 Wemos D1 mini
  Реализует вращение барабаном, подъем площадки, управление датчиком Холла
  Запитка по USB от Raspberry Pi 4b
  Сервопривод SG90
  Используется для переворота площадки
  Сервопривод постоянного вращения Feetech FTR90
  используется для вращения барабана
  Понижающий преоразователь DC DC LM2596
  Понижает и стабилизирует питание 7.4В -> 5В
  Кнопка питания
  Аккумулятор Li-ion 18650 2s 2p
  Питание устройства
  Датчики Холла A3144E
  Используются для отслеживания положения барабана
  Концевик RAMPS 1.4
  Используется для отслеживания момента полного опускания подъемной площадки
  Модуль контроля зарядки TP4056
  Конденсатор
  Шунтирует питание системы и дейтвует как местный источник питания
  Сервопривод постоянного вращения Feetech FTR90
  используется для перемещения подъемной площадки
  Кнопка питания
  1NO 1NC DPST
  Raspberry Pi 3 Model B+.
  Соединяется с Raspberry Pi по шине CIS

custom parts:
  Rasberry Pi NIOR Camera: Camera
  LM2596 step down module: LM2596 DC-DC step down power supply module 3 A.
  Limit Switch: Generic limit switch commonly found on 3D printers. Typical lever microswitch mounted on a PCB board with a 3 pin JST XH connector.
  TP4056: A DIP stand-in part for whatever IC you want. With 6 pins on a 300mil dual inline package (DIP) footprint.
